// Logisim project Atividade 9.circ as structural Verilog: 2 circuits, main circuit main
module main (
  input  in_1
);

  wire b0_out, b1_out, b2_out, b3_out, b4_out, b5_out, b6_out, b7_out, numeroA_p1, numeroA_p2, numeroA_p3,
       numeroA_p4, numeroA_p5, numeroA_p6, numeroA_p7, numeroA_p8, numeroB_p1, numeroB_p2, numeroB_p3,
       numeroB_p4, numeroB_p5, numeroB_p6, numeroB_p7, numeroB_p8, somador_completo_1_c1,
       somador_completo_1_s0, somador_completo_2_c1, somador_completo_2_s0, somador_completo_3_c1,
       somador_completo_3_s0, somador_completo_4_c1, somador_completo_4_s0, somador_completo_5_c1,
       somador_completo_5_s0, somador_completo_6_c1, somador_completo_6_s0, somador_completo_7_c1,
       somador_completo_7_s0, somador_completo_8_c1, somador_completo_8_s0, xor_1_out;

  xor xor_1 (xor_1_out, somador_completo_1_c1, somador_completo_2_c1);
  LED led_1 (.in(xor_1_out));
  xor b7 (b7_out, in_1, numeroB_p1);
  somador_completo somador_completo_1 (
    .a(numeroA_p1), .b(b7_out), .c0(somador_completo_2_c1), .c1(somador_completo_1_c1),
    .s0(somador_completo_1_s0));
  LED led_2 (.in(somador_completo_1_s0));
  xor b6 (b6_out, in_1, numeroB_p2);
  somador_completo somador_completo_2 (
    .a(numeroA_p2), .b(b6_out), .c0(somador_completo_3_c1), .c1(somador_completo_2_c1),
    .s0(somador_completo_2_s0));
  LED led_3 (.in(somador_completo_2_s0));
  LED led_4 (.in(somador_completo_3_s0));
  xor b5 (b5_out, in_1, numeroB_p3);
  somador_completo somador_completo_3 (
    .a(numeroA_p3), .b(b5_out), .c0(somador_completo_4_c1), .c1(somador_completo_3_c1),
    .s0(somador_completo_3_s0));
  xor b4 (b4_out, in_1, numeroB_p4);
  somador_completo somador_completo_4 (
    .a(numeroA_p4), .b(b4_out), .c0(somador_completo_5_c1), .c1(somador_completo_4_c1),
    .s0(somador_completo_4_s0));
  LED led_5 (.in(somador_completo_4_s0));
  // DipSwitch numeroA: pin names not known; wires that end beside it: numeroA_p1, numeroA_p2, numeroA_p3, numeroA_p4, numeroA_p5, numeroA_p6, numeroA_p7, numeroA_p8
  xor b3 (b3_out, in_1, numeroB_p5);
  somador_completo somador_completo_5 (
    .a(numeroA_p5), .b(b3_out), .c0(somador_completo_6_c1), .c1(somador_completo_5_c1),
    .s0(somador_completo_5_s0));
  LED led_6 (.in(somador_completo_5_s0));
  xor b2 (b2_out, in_1, numeroB_p6);
  somador_completo somador_completo_6 (
    .a(numeroA_p6), .b(b2_out), .c0(somador_completo_7_c1), .c1(somador_completo_6_c1),
    .s0(somador_completo_6_s0));
  LED led_7 (.in(somador_completo_6_s0));
  LED led_8 (.in(somador_completo_7_s0));
  xor b1 (b1_out, in_1, numeroB_p7);
  somador_completo somador_completo_7 (
    .a(numeroA_p7), .b(b1_out), .c0(somador_completo_8_c1), .c1(somador_completo_7_c1),
    .s0(somador_completo_7_s0));
  // DipSwitch numeroB: pin names not known; wires that end beside it: numeroB_p1, numeroB_p2, numeroB_p3, numeroB_p4, numeroB_p5, numeroB_p6, numeroB_p7, numeroB_p8
  xor b0 (b0_out, in_1, numeroB_p8);
  somador_completo somador_completo_8 (
    .a(numeroA_p8), .b(b0_out), .c0(in_1), .c1(somador_completo_8_c1), .s0(somador_completo_8_s0));
  LED led_9 (.in(somador_completo_8_s0));

  // Notes on the sheet:
  //   a7
  //   ON - overflow
  //   a6
  //   a5
  //   a4
  //   a3
  //   a2
  //   a1
  //   a0
  //   0 - SOMA
  //   1 - SUBTRAÇÃO
endmodule

module somador_completo (
  input  a,
  input  b,
  input  c0,
  output c1,
  output s0
);

  wire and_1_out, and_2_out, and_3_out, xor_1_out;

  and and_1 (and_1_out, b, c0);
  and and_2 (and_2_out, a, c0);
  or or_1 (c1, and_1_out, and_2_out, and_3_out);
  and and_3 (and_3_out, a, b);
  xor xor_1 (xor_1_out, a, b);
  xor xor_2 (s0, c0, xor_1_out);
endmodule
