// Logisim project Trabalho_CircuitosDigitais.circ as structural Verilog: 1 circuit, main circuit main
module main (
  input  Disparar
);

  wire a1_out, a_out, and_1_out, and_2_out, and_3_out, and_4_out, and_5_out, and_6_out, and_7_out, and_8_out,
       and_9_out, and_10_out, and_11_out, and_12_out, and_13_out, and_14_out, and_15_out, and_16_out,
       and_17_out, and_18_out, and_19_out, and_20_out, and_21_out, and_22_out, and_23_out, and_24_out,
       and_25_out, and_26_out, and_27_out, and_28_out, and_29_out, and_30_out, and_31_out, and_32_out,
       and_33_out, and_34_out, and_35_out, and_36_out, and_37_out, and_38_out, and_39_out, and_40_out,
       and_41_out, and_42_out, and_43_out, b1_out, b_out, c1_out, c_out, d1_out, d_out, dipswitch_1_sw1,
       dipswitch_1_sw2, dipswitch_1_sw3, dipswitch_1_sw4, dipswitch_2_sw1, dipswitch_2_sw2, dipswitch_2_sw3,
       dipswitch_2_sw4, dipswitch_3_sw1, dipswitch_3_sw2, dipswitch_3_sw3, dipswitch_3_sw4, not_1_out,
       not_2_out, not_3_out, not_4_out, not_5_out, not_6_out, not_7_out, not_8_out, not_9_out, not_10_out,
       not_11_out, not_12_out, not_13_out, not_14_out, not_15_out, not_16_out, not_17_out, not_18_out,
       not_19_out, not_20_out, not_21_out, not_22_out, not_23_out, not_24_out, not_25_out, not_26_out,
       not_27_out, not_28_out, not_29_out, not_30_out, not_31_out, not_32_out, not_33_out, not_34_out,
       not_35_out, not_36_out, not_37_out, not_38_out, not_39_out, not_40_out, not_41_out, not_42_out,
       not_43_out, not_44_out, not_45_out, not_46_out, not_47_out, not_48_out, not_49_out, not_50_out,
       not_51_out, or_1_out, xnor_1_out, xnor_2_out, xnor_3_out, xnor_4_out, xnor_5_out, xnor_6_out,
       xnor_7_out, xnor_8_out;

  not not_1 (not_1_out, dipswitch_1_sw3);
  not not_2 (not_2_out, dipswitch_1_sw4);
  not not_3 (not_3_out, dipswitch_1_sw1);
  not not_4 (not_4_out, dipswitch_1_sw2);
  and and_1 (and_1_out, dipswitch_1_sw3, not_5_out);
  not not_5 (not_5_out, dipswitch_1_sw4);
  not not_6 (not_6_out, dipswitch_1_sw1);
  not not_7 (not_7_out, dipswitch_1_sw4);
  not not_8 (not_8_out, dipswitch_1_sw1);
  not not_9 (not_9_out, dipswitch_1_sw4);
  not not_10 (not_10_out, dipswitch_1_sw3);
  not not_11 (not_11_out, dipswitch_1_sw2);
  not not_12 (not_12_out, dipswitch_1_sw3);
  not not_13 (not_13_out, dipswitch_1_sw4);
  not not_14 (not_14_out, dipswitch_1_sw1);
  not not_15 (not_15_out, dipswitch_1_sw1);
  not not_16 (not_16_out, dipswitch_1_sw3);
  not not_17 (not_17_out, dipswitch_1_sw4);
  not not_18 (not_18_out, dipswitch_1_sw3);
  not not_19 (not_19_out, dipswitch_1_sw1);
  not not_20 (not_20_out, dipswitch_1_sw2);
  not not_21 (not_21_out, dipswitch_1_sw3);
  not not_22 (not_22_out, dipswitch_1_sw1);
  not not_23 (not_23_out, dipswitch_1_sw4);
  not not_24 (not_24_out, dipswitch_1_sw2);
  not not_25 (not_25_out, dipswitch_1_sw4);
  DipSwitch #(.number(4)) dipswitch_1 (
    .sw1(dipswitch_1_sw1), .sw2(dipswitch_1_sw2), .sw3(dipswitch_1_sw3), .sw4(dipswitch_1_sw4));
  and and_2 (and_2_out, dipswitch_1_sw2, not_1_out, not_2_out);
  and and_3 (and_3_out, not_3_out, dipswitch_1_sw2, dipswitch_1_sw4);
  and and_4 (and_4_out, dipswitch_1_sw1, dipswitch_1_sw2, dipswitch_1_sw3);
  and and_5 (and_5_out, not_4_out, and_1_out);
  and and_6 (and_6_out, not_6_out, dipswitch_1_sw3);
  and and_7 (and_7_out, dipswitch_1_sw2, dipswitch_1_sw3, not_7_out);
  and and_8 (and_8_out, not_8_out, dipswitch_1_sw2, not_9_out);
  and and_9 (and_9_out, dipswitch_1_sw1, dipswitch_1_sw2, not_10_out, dipswitch_1_sw4);
  and and_10 (and_10_out, dipswitch_1_sw1, not_11_out, not_12_out, not_13_out);
  and and_11 (and_11_out, dipswitch_1_sw2, dipswitch_1_sw4);
  and and_12 (and_12_out, not_14_out, dipswitch_1_sw2);
  and and_13 (and_13_out, not_15_out, not_16_out, not_17_out);
  and and_14 (and_14_out, dipswitch_1_sw1, not_18_out, dipswitch_1_sw4);
  and and_15 (and_15_out, not_19_out, not_20_out, not_21_out);
  and and_16 (and_16_out, not_22_out, dipswitch_1_sw2, dipswitch_1_sw4);
  and and_17 (and_17_out, dipswitch_1_sw2, dipswitch_1_sw3, not_23_out);
  and and_18 (and_18_out, dipswitch_1_sw1, not_24_out, not_25_out);
  or a1 (a1_out, and_5_out, and_4_out, and_3_out, and_2_out);
  xnor xnor_1 (xnor_1_out, a1_out, and_20_out);
  or b1 (b1_out, and_10_out, and_9_out, and_8_out, and_7_out, and_6_out);
  xnor xnor_2 (xnor_2_out, b1_out, and_22_out);
  or c1 (c1_out, and_14_out, and_13_out, and_12_out, and_11_out);
  xnor xnor_3 (xnor_3_out, c1_out, and_23_out);
  and and_19 (and_19_out, xnor_1_out, xnor_2_out, xnor_3_out, xnor_4_out);
  or d1 (d1_out, and_18_out, and_17_out, and_16_out, and_15_out);
  xnor xnor_4 (xnor_4_out, d1_out, and_42_out);
  and and_20 (and_20_out, Disparar, dipswitch_3_sw1);
  and and_21 (and_21_out, Disparar, not_26_out);
  not not_26 (not_26_out, or_1_out);
  not not_27 (not_27_out, dipswitch_2_sw3);
  not not_28 (not_28_out, dipswitch_2_sw4);
  not not_29 (not_29_out, dipswitch_2_sw1);
  not not_30 (not_30_out, dipswitch_2_sw2);
  not not_31 (not_31_out, dipswitch_2_sw4);
  not not_32 (not_32_out, dipswitch_2_sw1);
  not not_33 (not_33_out, dipswitch_2_sw4);
  not not_34 (not_34_out, dipswitch_2_sw1);
  not not_35 (not_35_out, dipswitch_2_sw4);
  not not_36 (not_36_out, dipswitch_2_sw3);
  not not_37 (not_37_out, dipswitch_2_sw2);
  not not_38 (not_38_out, dipswitch_2_sw3);
  not not_39 (not_39_out, dipswitch_2_sw4);
  not not_40 (not_40_out, dipswitch_2_sw1);
  not not_41 (not_41_out, dipswitch_2_sw1);
  not not_42 (not_42_out, dipswitch_2_sw3);
  not not_43 (not_43_out, dipswitch_2_sw4);
  not not_44 (not_44_out, dipswitch_2_sw3);
  not not_45 (not_45_out, dipswitch_2_sw1);
  not not_46 (not_46_out, dipswitch_2_sw2);
  not not_47 (not_47_out, dipswitch_2_sw3);
  not not_48 (not_48_out, dipswitch_2_sw1);
  not not_49 (not_49_out, dipswitch_2_sw4);
  not not_50 (not_50_out, dipswitch_2_sw2);
  not not_51 (not_51_out, dipswitch_2_sw4);
  DipSwitch #(.number(4)) dipswitch_2 (
    .sw1(dipswitch_2_sw1), .sw2(dipswitch_2_sw2), .sw3(dipswitch_2_sw3), .sw4(dipswitch_2_sw4));
  and and_22 (and_22_out, Disparar, dipswitch_3_sw2);
  and and_23 (and_23_out, Disparar, dipswitch_3_sw3);
  DipSwitch #(.number(4)) dipswitch_3 (
    .sw1(dipswitch_3_sw1), .sw2(dipswitch_3_sw2), .sw3(dipswitch_3_sw3), .sw4(dipswitch_3_sw4));
  LED led_1 (.in(and_21_out));
  LED led_2 (.in(or_1_out));
  or or_1 (or_1_out, and_19_out, and_43_out);
  and and_24 (and_24_out, dipswitch_2_sw2, not_27_out, not_28_out);
  and and_25 (and_25_out, not_29_out, dipswitch_2_sw2, dipswitch_2_sw4);
  and and_26 (and_26_out, dipswitch_2_sw1, dipswitch_2_sw2, dipswitch_2_sw3);
  and and_27 (and_27_out, not_30_out, and_28_out);
  and and_28 (and_28_out, dipswitch_2_sw3, not_31_out);
  and and_29 (and_29_out, not_32_out, dipswitch_2_sw3);
  and and_30 (and_30_out, dipswitch_2_sw2, dipswitch_2_sw3, not_33_out);
  and and_31 (and_31_out, not_34_out, dipswitch_2_sw2, not_35_out);
  and and_32 (and_32_out, dipswitch_2_sw1, dipswitch_2_sw2, not_36_out, dipswitch_2_sw4);
  and and_33 (and_33_out, dipswitch_2_sw1, not_37_out, not_38_out, not_39_out);
  and and_34 (and_34_out, dipswitch_2_sw2, dipswitch_2_sw4);
  and and_35 (and_35_out, not_40_out, dipswitch_2_sw2);
  and and_36 (and_36_out, not_41_out, not_42_out, not_43_out);
  and and_37 (and_37_out, dipswitch_2_sw1, not_44_out, dipswitch_2_sw4);
  and and_38 (and_38_out, not_45_out, not_46_out, not_47_out);
  and and_39 (and_39_out, not_48_out, dipswitch_2_sw2, dipswitch_2_sw4);
  and and_40 (and_40_out, dipswitch_2_sw2, dipswitch_2_sw3, not_49_out);
  and and_41 (and_41_out, dipswitch_2_sw1, not_50_out, not_51_out);
  and and_42 (and_42_out, Disparar, dipswitch_3_sw4);
  or a (a_out, and_27_out, and_26_out, and_25_out, and_24_out);
  or b (b_out, and_33_out, and_32_out, and_31_out, and_30_out, and_29_out);
  xnor xnor_5 (xnor_5_out, a_out, and_20_out);
  xnor xnor_6 (xnor_6_out, b_out, and_22_out);
  or c (c_out, and_37_out, and_36_out, and_35_out, and_34_out);
  xnor xnor_7 (xnor_7_out, c_out, and_23_out);
  and and_43 (and_43_out, xnor_5_out, xnor_6_out, xnor_7_out, xnor_8_out);
  or d (d_out, and_41_out, and_40_out, and_39_out, and_38_out);
  xnor xnor_8 (xnor_8_out, d_out, and_42_out);

  // Notes on the sheet:
  //   Navio 1
  //   <-A->
  //   <-B->
  //   <-C->
  //   <-D->
  //   Navio 2
  //   Alvo
  //   Errou!
  //   Acertou!
  //   1
  //   2
  //   4
  //   3
endmodule
