// Logisim project Trabalho 2 - Banco de Regs + ULA.circ as structural Verilog: 1 circuit, main circuit main
module main (
  input  in_1
);

  wire adder_1_cout, adder_2_cout, adder_3_cout, adder_4_cout, adder_5_cout, adder_6_cout, adder_7_cout,
       adder_8_cout, and_1_out, and_2_out, and_3_out, and_4_out, and_13_out, Escreve_out, not_1_out,
       not_2_out, not_3_out, not_4_out, not_13_out, not_14_out, not_15_out, not_16_out, not_17_out,
       not_18_out, not_19_out, not_20_out, xnor_1_out, xnor_2_out, xnor_3_out, xnor_4_out, xnor_5_out,
       xnor_6_out, xnor_7_out, xnor_8_out, xor_1_out, xor_2_out, xor_3_out, xor_4_out, xor_5_out, xor_6_out,
       xor_7_out, xor_8_out, xor_9_out;
  wire [1:0] undriven, undriven_3, undriven_4;
  wire [2:0] undriven_2;
  wire [7:0] adder_1_out, and_12_out, demultiplexer_1_out0, demultiplexer_1_out1, demultiplexer_1_out2,
       demultiplexer_1_out3, dipswitch_1_p8, multiplexer_1_out, multiplexer_2_out, multiplexer_3_out,
       multiplexer_4_out, nand_8_out, nor_8_out, not_12_out, not_28_out, R0_q, R1_q, R2_q, R3_q;

  not not_1 (not_1_out, undriven[1]);
  not not_2 (not_2_out, undriven[0]);
  not not_3 (not_3_out, undriven[1]);
  Button Escreve (.out(Escreve_out));
  and and_1 (and_1_out, not_1_out, not_2_out, Escreve_out);
  not not_4 (not_4_out, undriven[0]);
  and and_2 (and_2_out, not_3_out, undriven[0], Escreve_out);
  and and_3 (and_3_out, undriven[1], not_4_out, Escreve_out);
  and and_4 (and_4_out, undriven[1], undriven[0], Escreve_out);
  Register R0 (.D(demultiplexer_1_out0), .clk(and_1_out), .Q(R0_q));  // open: en, clr
  Register R1 (.D(demultiplexer_1_out1), .clk(and_2_out), .Q(R1_q));  // open: en, clr
  Multiplexer #(.enable("false"), .select(2), .width(8)) multiplexer_1 (
    .in0(R0_q), .in1(R1_q), .in2(R2_q), .in3(R3_q), .out(multiplexer_1_out), .sel(undriven_3));
  nor nor_1 (nor_8_out[7], multiplexer_1_out[7], multiplexer_4_out[7]);
  Multiplexer #(.enable("false"), .width(8)) multiplexer_2 (
    .in0(multiplexer_3_out), .in1(dipswitch_1_p8), .out(multiplexer_2_out), .sel(in_1));
  Demultiplexer #(.enable("false"), .select(2), .width(8)) demultiplexer_1 (
    .out0(demultiplexer_1_out0), .out1(demultiplexer_1_out1), .out2(demultiplexer_1_out2),
    .out3(demultiplexer_1_out3), .in(multiplexer_2_out), .sel(undriven));
  nor nor_2 (nor_8_out[6], multiplexer_1_out[6], multiplexer_4_out[6]);
  nor nor_3 (nor_8_out[5], multiplexer_1_out[5], multiplexer_4_out[5]);
  // DipSwitch #(.number(3)) SelOP: pin names not known
  Register R2 (.D(demultiplexer_1_out2), .clk(and_3_out), .Q(R2_q));  // open: en, clr
  nor nor_4 (nor_8_out[4], multiplexer_1_out[4], multiplexer_4_out[4]);
  nor nor_5 (nor_8_out[3], multiplexer_1_out[3], multiplexer_4_out[3]);
  nor nor_6 (nor_8_out[2], multiplexer_1_out[2], multiplexer_4_out[2]);
  // DipSwitch dipswitch_1: pin names not known; wires that end beside it: dipswitch_1_p8[7], dipswitch_1_p8[6], dipswitch_1_p8[5], dipswitch_1_p8[4], dipswitch_1_p8[3], dipswitch_1_p8[2], dipswitch_1_p8[1], dipswitch_1_p8[0]
  // DipSwitch #(.number(2)) SelRW: pin names not known
  Register R3 (.D(demultiplexer_1_out3), .clk(and_4_out), .Q(R3_q));  // open: en, clr
  nor nor_7 (nor_8_out[1], multiplexer_1_out[1], multiplexer_4_out[1]);
  nor nor_8 (nor_8_out[0], multiplexer_1_out[0], multiplexer_4_out[0]);
  Multiplexer #(.enable("false"), .select(3), .width(8)) multiplexer_3 (
    .in0(nor_8_out), .in1(and_12_out), .in2(not_12_out), .in3(adder_1_out), .in4(multiplexer_4_out),
    .in5(nand_8_out), .in6(not_12_out), .in7(not_28_out), .out(multiplexer_3_out), .sel(undriven_2));
  LED led_1 (.in(multiplexer_3_out[7]));
  // DipSwitch #(.number(2)) SelRA: pin names not known
  Multiplexer #(.enable("false"), .select(2), .width(8)) multiplexer_4 (
    .in0(R0_q), .in1(R1_q), .in2(R2_q), .in3(R3_q), .out(multiplexer_4_out), .sel(undriven_4));
  and and_5 (and_12_out[7], multiplexer_1_out[7], multiplexer_4_out[7]);
  and and_6 (and_12_out[6], multiplexer_1_out[6], multiplexer_4_out[6]);
  LED led_2 (.in(multiplexer_3_out[6]));
  LED led_3 (.in(multiplexer_3_out[5]));
  LED led_4 (.in(multiplexer_3_out[4]));
  // DipSwitch #(.number(2)) SelRB: pin names not known
  and and_7 (and_12_out[5], multiplexer_1_out[5], multiplexer_4_out[5]);
  and and_8 (and_12_out[4], multiplexer_1_out[4], multiplexer_4_out[4]);
  and and_9 (and_12_out[3], multiplexer_1_out[3], multiplexer_4_out[3]);
  LED led_5 (.in(multiplexer_3_out[3]));
  LED led_6 (.in(multiplexer_3_out[2]));
  and and_10 (and_12_out[2], multiplexer_1_out[2], multiplexer_4_out[2]);
  and and_11 (and_12_out[1], multiplexer_1_out[1], multiplexer_4_out[1]);
  LED led_7 (.in(multiplexer_3_out[1]));
  LED led_8 (.in(multiplexer_3_out[0]));
  xnor xnor_1 (xnor_1_out, multiplexer_3_out[7], 1'b0);
  xnor xnor_2 (xnor_2_out, multiplexer_3_out[6], 1'b0);
  xnor xnor_3 (xnor_3_out, multiplexer_3_out[5], 1'b0);
  not not_5 (not_12_out[7], multiplexer_1_out[7]);
  and and_12 (and_12_out[0], multiplexer_1_out[0], multiplexer_4_out[0]);
  xor xor_1 (xor_1_out, adder_8_cout, adder_7_cout);
  LED led_9 (.in(xor_1_out));
  LED led_10 (.in(and_13_out));
  and and_13 (and_13_out, xnor_1_out, xnor_2_out, xnor_3_out, xnor_4_out, xnor_5_out, xnor_6_out, xnor_8_out, xnor_7_out);
  xnor xnor_4 (xnor_4_out, multiplexer_3_out[4], 1'b0);
  xnor xnor_5 (xnor_5_out, multiplexer_3_out[3], 1'b0);
  xnor xnor_6 (xnor_6_out, multiplexer_3_out[2], 1'b0);
  not not_6 (not_12_out[4], multiplexer_1_out[4]);
  not not_7 (not_12_out[6], multiplexer_1_out[6]);
  not not_8 (not_12_out[5], multiplexer_1_out[5]);
  xnor xnor_7 (xnor_7_out, multiplexer_3_out[0], 1'b0);
  xnor xnor_8 (xnor_8_out, multiplexer_3_out[1], 1'b0);
  not not_9 (not_12_out[3], multiplexer_1_out[3]);
  not not_10 (not_12_out[2], multiplexer_1_out[2]);
  not not_11 (not_12_out[1], multiplexer_1_out[1]);
  not not_12 (not_12_out[0], multiplexer_1_out[0]);
  Adder #(.width(1)) adder_1 (
    .a(multiplexer_1_out[0]), .b(not_13_out), .out(adder_1_out[0]), .cin(1'b1), .cout(adder_1_cout));
  not not_13 (not_13_out, multiplexer_4_out[0]);
  Adder #(.width(1)) adder_2 (
    .a(multiplexer_1_out[1]), .b(not_14_out), .out(adder_1_out[1]), .cin(adder_1_cout), .cout(adder_2_cout));
  not not_14 (not_14_out, multiplexer_4_out[1]);
  Adder #(.width(1)) adder_3 (
    .a(multiplexer_1_out[2]), .b(not_15_out), .out(adder_1_out[2]), .cin(adder_2_cout), .cout(adder_3_cout));
  not not_15 (not_15_out, multiplexer_4_out[2]);
  Adder #(.width(1)) adder_4 (
    .a(multiplexer_1_out[3]), .b(not_16_out), .out(adder_1_out[3]), .cin(adder_3_cout), .cout(adder_4_cout));
  not not_16 (not_16_out, multiplexer_4_out[3]);
  Adder #(.width(1)) adder_5 (
    .a(multiplexer_1_out[4]), .b(not_17_out), .out(adder_1_out[4]), .cin(adder_4_cout), .cout(adder_5_cout));
  not not_17 (not_17_out, multiplexer_4_out[4]);
  Adder #(.width(1)) adder_6 (
    .a(multiplexer_1_out[5]), .b(not_18_out), .out(adder_1_out[5]), .cin(adder_5_cout), .cout(adder_6_cout));
  not not_18 (not_18_out, multiplexer_4_out[5]);
  Adder #(.width(1)) adder_7 (
    .a(multiplexer_1_out[6]), .b(not_19_out), .out(adder_1_out[6]), .cin(adder_6_cout), .cout(adder_7_cout));
  not not_19 (not_19_out, multiplexer_4_out[6]);
  Adder #(.width(1)) adder_8 (
    .a(multiplexer_1_out[7]), .b(not_20_out), .out(adder_1_out[7]), .cin(adder_7_cout), .cout(adder_8_cout));
  not not_20 (not_20_out, multiplexer_4_out[7]);
  nand nand_1 (nand_8_out[7], multiplexer_1_out[7], multiplexer_4_out[7]);
  nand nand_2 (nand_8_out[6], multiplexer_1_out[6], multiplexer_4_out[6]);
  nand nand_3 (nand_8_out[5], multiplexer_1_out[5], multiplexer_4_out[5]);
  nand nand_4 (nand_8_out[4], multiplexer_1_out[4], multiplexer_4_out[4]);
  nand nand_5 (nand_8_out[3], multiplexer_1_out[3], multiplexer_4_out[3]);
  nand nand_6 (nand_8_out[2], multiplexer_1_out[2], multiplexer_4_out[2]);
  nand nand_7 (nand_8_out[1], multiplexer_1_out[1], multiplexer_4_out[1]);
  nand nand_8 (nand_8_out[0], multiplexer_1_out[0], multiplexer_4_out[0]);
  xor xor_2 (xor_2_out, multiplexer_1_out[7], multiplexer_4_out[7]);
  xor xor_3 (xor_3_out, multiplexer_1_out[6], multiplexer_4_out[6]);
  not not_21 (not_28_out[7], xor_2_out);
  not not_22 (not_28_out[6], xor_3_out);
  xor xor_4 (xor_4_out, multiplexer_1_out[5], multiplexer_4_out[5]);
  xor xor_5 (xor_5_out, multiplexer_1_out[4], multiplexer_4_out[4]);
  xor xor_6 (xor_6_out, multiplexer_1_out[3], multiplexer_4_out[3]);
  not not_23 (not_28_out[5], xor_4_out);
  not not_24 (not_28_out[4], xor_5_out);
  not not_25 (not_28_out[3], xor_6_out);
  xor xor_7 (xor_7_out, multiplexer_1_out[2], multiplexer_4_out[2]);
  xor xor_8 (xor_8_out, multiplexer_1_out[1], multiplexer_4_out[1]);
  not not_26 (not_28_out[2], xor_7_out);
  not not_27 (not_28_out[1], xor_8_out);
  xor xor_9 (xor_9_out, multiplexer_1_out[0], multiplexer_4_out[0]);
  not not_28 (not_28_out[0], xor_9_out);

  // Notes on the sheet:
  //   A
  //   A nor B
  //   B
  //   A and B
  //   ~A
  //   Overflow!
  //   Deu Zero!
  //   A-B
  //   B
  //   A nand B
  //   ~(A xor B)
endmodule
