// Logisim project Tarefa 2 - Circuito.circ as structural Verilog: 1 circuit, main circuit main
module main (
  input  cnt,
  output K
);

  wire and_1_out, and_2_out, and_3_out, clk_out, not_1_out, or_1_out, q0_q, q0_qn, q1_q, q1_qn, xor_1_out;

  not not_1 (not_1_out, cnt);
  Button clk (.out(clk_out));
  xor xor_1 (xor_1_out, q0_q, cnt);
  and and_1 (and_1_out, not_1_out, q1_q);
  and and_2 (and_2_out, q0_q, cnt, q1_qn);
  and and_3 (and_3_out, cnt, q1_q, q0_qn);
  or or_1 (or_1_out, and_1_out, and_2_out, and_3_out);
  D_Flip_Flop q0 (.D(xor_1_out), .clk(clk_out), .Q(q0_q), .Qn(q0_qn));  // open: preset, reset
  D_Flip_Flop q1 (.D(or_1_out), .clk(clk_out), .Q(q1_q), .Qn(q1_qn));  // open: preset, reset
  and and_4 (K, q0_q, q1_q);
endmodule
